// Logisim project shift register.circ as structural Verilog: 1 circuit, main circuit main
module main (
);

  wire clock_1_out, Input, Q0, Q1, Q2, Q3, Reset;

  Clock clock_1 (.out(clock_1_out));
  D_Flip_Flop d_ff_1 (.clk(clock_1_out), .D(Input), .Q(Q3), .en(Reset));  // open: Qn, preset, reset
  D_Flip_Flop d_ff_2 (.clk(clock_1_out), .D(Q3), .Q(Q2), .en(Reset));  // open: Qn, preset, reset
  D_Flip_Flop d_ff_3 (.clk(clock_1_out), .D(Q2), .Q(Q1), .en(Reset));  // open: Qn, preset, reset
  D_Flip_Flop d_ff_4 (.clk(clock_1_out), .D(Q1), .Q(Q0), .en(Reset));  // open: Qn, preset, reset
endmodule
