// Logisim project testgates.circ as structural Verilog: 1 circuit, main circuit main
module main (
);

  wire A, ANDOUT, B, C, D, ERROR1, ERROR2, NAND1_out, NAND2_out, NANDOUT, NOR1_out, NOR2_out, NOROUT, OROUT;

  nand NAND1 (NAND1_out, A, A);
  nand NAND2 (NAND2_out, B, B);
  nor NOR1 (NOR1_out, C, C);
  nor NOR2 (NOR2_out, D, D);
  or OR (OROUT, B, A);
  nand NAND3 (NANDOUT, NAND1_out, NAND2_out);
  and AND (ANDOUT, D, C);
  nor NOR3 (NOROUT, NOR1_out, NOR2_out);
  xor X1 (ERROR1, OROUT, NANDOUT);
  xor X2 (ERROR2, ANDOUT, NOROUT);
endmodule
