// Logisim project counter.circ as structural Verilog: 1 circuit, main circuit main
module main (
  output out_1
);

  wire _1, _2, _3, clock_1_out, d_ff_1_qn, d_ff_2_qn, d_ff_3_qn;

  Clock clock_1 (.out(clock_1_out));
  D_Flip_Flop d_ff_1 (.clk(clock_1_out), .D(d_ff_3_qn), .Q(_1), .Qn(d_ff_1_qn));  // open: preset, en, reset
  D_Flip_Flop d_ff_2 (.clk(clock_1_out), .D(d_ff_1_qn), .Q(_2), .Qn(d_ff_2_qn));  // open: preset, en, reset
  D_Flip_Flop d_ff_3 (.clk(clock_1_out), .D(d_ff_2_qn), .Q(_3), .Qn(d_ff_3_qn));  // open: preset, en, reset
endmodule
