// Logisim project grcode.circ as structural Verilog: 1 circuit, main circuit main
module main (
);

  wire A, and_1_out, and_2_out, and_3_out, and_4_out, B, C, CLK, JK2_qn, JK3_qn, undriven, xnor_1_out,
       xor_1_out;

  xnor xnor_1 (xnor_1_out, undriven, B);
  xor xor_1 (xor_1_out, C, B);
  J_K_Flip_Flop JK1 (.J(xnor_1_out), .clk(CLK), .K(xor_1_out), .Q(A));  // open: Qn, preset, en, reset
  and and_1 (and_1_out, JK3_qn, A);
  and and_2 (and_2_out, A, C);
  J_K_Flip_Flop JK2 (.J(and_1_out), .clk(CLK), .K(and_2_out), .Q(B), .Qn(JK2_qn));  // open: preset, en, reset
  and and_3 (and_3_out, undriven, B);
  and and_4 (and_4_out, JK2_qn, undriven);
  J_K_Flip_Flop JK3 (.J(and_3_out), .clk(CLK), .K(and_4_out), .Q(C), .Qn(JK3_qn));  // open: preset, en, reset
endmodule
