// Logisim project xorfromnand.circ as structural Verilog: 1 circuit, main circuit main
module main (
);

  wire A, B, nand_1_out, nand_2_out, nand_3_out, Out;

  nand nand_1 (nand_1_out, A, B);
  nand nand_2 (nand_2_out, A, nand_1_out);
  nand nand_3 (nand_3_out, nand_1_out, B);
  nand nand_4 (Out, nand_2_out, nand_3_out);
endmodule
